// Logisim project Acumuladores.circ as structural Verilog: 1 circuit, main circuit main
module main (
  input  [7:0] IN,
  input  OUT_CLK,
  input  IN_BUS,
  input  ACC_BUS,
  input  ACC_CLK,
  input  ACC_CIR
);

  wire [7:0] adder_1_out, controlled_buffer_1_out, OUT_q, register_1_q;

  Hex_Digit_Display hex_digit_display_1 (.value(IN[7:4]));  // open: dp
  Hex_Digit_Display hex_digit_display_2 (.value(IN[3:0]));  // open: dp
  assign controlled_buffer_1_out = IN_BUS ? IN : 8'bz;  // Controlled_Buffer controlled_buffer_1
  assign controlled_buffer_1_out = ACC_BUS ? register_1_q : 8'bz;  // Controlled_Buffer controlled_buffer_2
  Register #(.Select("low")) OUT (.D(controlled_buffer_1_out), .Q(OUT_q), .clk(OUT_CLK));  // open: en, clr
  Adder adder_1 (.a(register_1_q), .b(controlled_buffer_1_out), .out(adder_1_out));  // open: cin, cout
  Hex_Digit_Display hex_digit_display_3 (.value(OUT_q[3:0]));  // open: dp
  Hex_Digit_Display hex_digit_display_4 (.value(OUT_q[7:4]));  // open: dp
  Register #(.Select("low")) register_1 (.D(adder_1_out), .Q(register_1_q), .clk(ACC_CLK), .clr(ACC_CIR));  // open: en
endmodule
