// Logisim project Barramentos.circ as structural Verilog: 3 circuits, main circuit Q1
module Q1 (
  input  busC,
  input  clock_A,
  input  busA,
  input  clock_C,
  input  clock_B,
  input  busB,
  input  [7:0] entrada,
  input  busEntrada
);

  wire [7:0] controlled_buffer_1_out, register_1_q, register_2_q, register_3_q;

  Register #(.Select("low")) register_1 (
    .D(controlled_buffer_1_out), .Q(register_1_q), .clk(clock_A));  // open: en, clr
  Register #(.Select("low")) register_2 (
    .D(controlled_buffer_1_out), .Q(register_2_q), .clk(clock_B));  // open: en, clr
  assign controlled_buffer_1_out = busA ? register_1_q : 8'bz;  // Controlled_Buffer controlled_buffer_1
  assign controlled_buffer_1_out = busB ? register_2_q : 8'bz;  // Controlled_Buffer controlled_buffer_2
  assign controlled_buffer_1_out = busEntrada ? entrada : 8'bz;  // Controlled_Buffer controlled_buffer_3
  assign controlled_buffer_1_out = busC ? register_3_q : 8'bz;  // Controlled_Buffer controlled_buffer_4
  Register #(.Select("low")) register_3 (
    .D(controlled_buffer_1_out), .Q(register_3_q), .clk(clock_C));  // open: en, clr

  // Notes on the sheet:
  //   A
  //   B
  //   C
endmodule

module Q2 (
  input  busC,
  input  clock_A,
  input  busA,
  input  clock_C,
  input  clock_B,
  input  busB,
  input  [7:0] entrada,
  input  busEntrada
);

  wire [7:0] controlled_buffer_1_out, register_1_q, register_2_q, register_3_q;

  Register #(.Select("low")) register_1 (
    .D(controlled_buffer_1_out), .Q(register_1_q), .clk(clock_A));  // open: en, clr
  Register #(.Select("low")) register_2 (
    .D(controlled_buffer_1_out), .Q(register_2_q), .clk(clock_B));  // open: en, clr
  assign controlled_buffer_1_out = busA ? register_1_q : 8'bz;  // Controlled_Buffer controlled_buffer_1
  assign controlled_buffer_1_out = busB ? register_2_q : 8'bz;  // Controlled_Buffer controlled_buffer_2
  assign controlled_buffer_1_out = busEntrada ? entrada : 8'bz;  // Controlled_Buffer controlled_buffer_3
  assign controlled_buffer_1_out = busC ? register_3_q : 8'bz;  // Controlled_Buffer controlled_buffer_4
  Register #(.Select("low")) register_3 (
    .D(controlled_buffer_1_out), .Q(register_3_q), .clk(clock_C));  // open: en, clr

  // Notes on the sheet:
  //   A
  //   B
  //   C
endmodule

module Q3 (
  input  busC,
  input  busC_2,
  input  clock_A,
  input  busA,
  input  clock_A_2,
  input  busA_2,
  input  clock_C,
  input  clock_C_2,
  input  clock_B,
  input  busB,
  input  clock_B_2,
  input  busB_2,
  input  [7:0] entrada,
  input  [7:0] entrada_2,
  input  busEntrada,
  input  busEntrada_2
);

  wire [7:0] controlled_buffer_1_out, controlled_buffer_5_out, register_1_q, register_2_q, register_3_q,
       register_4_q, register_5_q, register_6_q;

  Register #(.Select("low")) register_1 (
    .D(controlled_buffer_1_out), .Q(register_1_q), .clk(clock_A));  // open: en, clr
  Register #(.Select("low")) register_2 (
    .D(controlled_buffer_1_out), .Q(register_2_q), .clk(clock_B));  // open: en, clr
  assign controlled_buffer_1_out = busA ? register_1_q : 8'bz;  // Controlled_Buffer controlled_buffer_1
  assign controlled_buffer_1_out = busB ? register_2_q : 8'bz;  // Controlled_Buffer controlled_buffer_2
  assign controlled_buffer_1_out = busEntrada ? entrada : 8'bz;  // Controlled_Buffer controlled_buffer_3
  assign controlled_buffer_1_out = busC ? register_3_q : 8'bz;  // Controlled_Buffer controlled_buffer_4
  Register #(.Select("low")) register_3 (
    .D(controlled_buffer_1_out), .Q(register_3_q), .clk(clock_C));  // open: en, clr
  Register #(.Select("low")) register_4 (
    .D(controlled_buffer_5_out), .Q(register_4_q), .clk(clock_A_2));  // open: en, clr
  Register #(.Select("low")) register_5 (
    .D(controlled_buffer_5_out), .Q(register_5_q), .clk(clock_B_2));  // open: en, clr
  assign controlled_buffer_5_out = busA_2 ? register_4_q : 8'bz;  // Controlled_Buffer controlled_buffer_5
  assign controlled_buffer_5_out = busB_2 ? register_5_q : 8'bz;  // Controlled_Buffer controlled_buffer_6
  assign controlled_buffer_5_out = busEntrada_2 ? entrada_2 : 8'bz;  // Controlled_Buffer controlled_buffer_7
  assign controlled_buffer_5_out = busC_2 ? register_6_q : 8'bz;  // Controlled_Buffer controlled_buffer_8
  Register #(.Select("low")) register_6 (
    .D(controlled_buffer_5_out), .Q(register_6_q), .clk(clock_C_2));  // open: en, clr

  // Notes on the sheet:
  //   A
  //   B
  //   CASO 1
  //   C
  //   CASO 2
  //   A
  //   B
  //   C
endmodule
