// Logisim project Calculadora.circ as structural Verilog: 2 circuits, main circuit Q1
module Q1 (
  input  OUT_clk,
  input  [15:0] Input,
  input  IN_bus,
  input  IN_clk,
  input  DR_bus,
  input  DR_clk,
  input  MAR_clk,
  input  RAM_clk,
  input  RAM_bus,
  input  ACC_bus,
  input  ACC_clk,
  input  ACC_clear,
  output [15:0] Output,
  output A___In,
  output out_15,
  output B___ACC
);

  wire [15:0] ACC_q, adder_1_out, controlled_buffer_1_out, MAR_q, register_1_q, register_2_q;

  Register #(.width(16), .Select("low")) MAR (.D(controlled_buffer_1_out), .Q(MAR_q), .clk(MAR_clk));  // open: en, clr
  Register #(.width(16), .Select("low")) register_1 (.D(Input), .Q(register_1_q), .clk(IN_clk));  // open: en, clr
  assign controlled_buffer_1_out = IN_bus ? register_1_q : 16'bz;  // Controlled_Buffer controlled_buffer_1
  RAM #(.addrWidth(16), .dataWidth(16), .Select("low")) ram_1 (
    .addr(MAR_q), .data(controlled_buffer_1_out), .clk(RAM_clk), .ld(RAM_bus));  // open: sel, clr
  assign controlled_buffer_1_out = ACC_bus ? ACC_q : 16'bz;  // Controlled_Buffer controlled_buffer_2
  assign controlled_buffer_1_out = DR_bus ? register_2_q : 16'bz;  // Controlled_Buffer controlled_buffer_3
  Register #(.width(16), .Select("low")) register_2 (
    .D(controlled_buffer_1_out), .Q(register_2_q), .clk(DR_clk));  // open: en, clr
  Register #(.width(16), .Select("low")) register_3 (
    .D(controlled_buffer_1_out), .Q(Output), .clk(OUT_clk));  // open: en, clr
  Adder #(.width(16)) adder_1 (.a(controlled_buffer_1_out), .b(ACC_q), .out(adder_1_out));  // open: cin, cout
  Comparator #(.width(16)) comparator_1 (
    .a(controlled_buffer_1_out), .b(ACC_q), .gt(A___In), .eq(out_15), .lt(B___ACC));
  Register #(.width(16), .Select("low")) ACC (.D(adder_1_out), .Q(ACC_q), .clk(ACC_clk), .clr(ACC_clear));  // open: en
endmodule

module Q2 (
  input  OUT_clk,
  input  [15:0] Input,
  input  IN_bus,
  input  IN_clk,
  input  DR_bus,
  input  DR_clk,
  input  MAR_clk,
  input  RAM_clk,
  input  RAM_bus,
  input  ACC_bus,
  input  ACC_clk,
  input  ACC_clear,
  output [15:0] Output,
  output A___In,
  output out_15,
  output B___ACC
);

  wire [15:0] ACC_q, controlled_buffer_1_out, IN_q, MAR_q, register_1_q, subtractor_1_out;

  Register #(.width(16), .Select("low")) MAR (.D(controlled_buffer_1_out), .Q(MAR_q), .clk(MAR_clk));  // open: en, clr
  Register #(.width(16), .Select("low")) IN (.D(Input), .Q(IN_q), .clk(IN_clk));  // open: en, clr
  assign controlled_buffer_1_out = IN_bus ? IN_q : 16'bz;  // Controlled_Buffer controlled_buffer_1
  RAM #(.addrWidth(16), .dataWidth(16), .Select("low")) ram_1 (
    .addr(MAR_q), .data(controlled_buffer_1_out), .clk(RAM_clk), .ld(RAM_bus));  // open: sel, clr
  assign controlled_buffer_1_out = ACC_bus ? ACC_q : 16'bz;  // Controlled_Buffer controlled_buffer_2
  assign controlled_buffer_1_out = DR_bus ? register_1_q : 16'bz;  // Controlled_Buffer controlled_buffer_3
  Register #(.width(16), .Select("low")) register_1 (
    .D(controlled_buffer_1_out), .Q(register_1_q), .clk(DR_clk));  // open: en, clr
  Register #(.width(16), .Select("low")) register_2 (
    .D(controlled_buffer_1_out), .Q(Output), .clk(OUT_clk));  // open: en, clr
  Subtractor #(.width(16)) subtractor_1 (
    .a(controlled_buffer_1_out), .b(ACC_q), .out(subtractor_1_out));  // open: bin, bout
  Comparator #(.width(16)) comparator_1 (
    .a(controlled_buffer_1_out), .b(ACC_q), .gt(A___In), .eq(out_15), .lt(B___ACC));
  Register #(.width(16), .trigger("falling"), .Select("low")) ACC (
    .D(subtractor_1_out), .Q(ACC_q), .clk(ACC_clk), .clr(ACC_clear));  // open: en
endmodule
