// Logisim project Clock.circ as structural Verilog: 1 circuit, main circuit main
module main (
  input  Reset,
  output T0,
  output T1,
  output T2
);

  wire Clock_out;

  Clock Clock (.out(Clock_out));
  D_Flip_Flop #(.Pre_Clr_Positions("LEGACY"), .enable("true"), .NewFFLayout("false")) u_T0 (
    .clk(Clock_out), .D(T2), .Q(T0), .preset(Reset));  // open: Qn, en, reset
  // Digital_Oscilloscope digital_oscilloscope_1: pin names not known; wires that end beside it: Clock_out, T0, T1, T2, Reset
  D_Flip_Flop #(.Pre_Clr_Positions("LEGACY"), .enable("true"), .NewFFLayout("false")) u_T1 (
    .clk(Clock_out), .D(T0), .Q(T1), .reset(Reset));  // open: Qn, preset, en
  D_Flip_Flop #(.Pre_Clr_Positions("LEGACY"), .enable("true"), .NewFFLayout("false")) u_T2 (
    .clk(Clock_out), .D(T1), .Q(T2), .reset(Reset));  // open: Qn, preset, en

  // Notes on the sheet:
  //   Clock
  //   T0
  //   T1
  //   T2
  //   Reset
endmodule
