// Logisim project Contador_0-13.circ as structural Verilog: 1 circuit, main circuit main
module main (
  input  in_1,
  input  in_2,
  output out_3,
  output out_4,
  output out_5,
  output out_6
);

  wire and_1_out, clock_1_out;

  Clock clock_1 (.out(clock_1_out));
  J_K_Flip_Flop #(.trigger("falling")) j_k_ff_1 (
    .J(in_1), .clk(clock_1_out), .K(in_2), .Q(out_3), .preset(and_1_out));  // open: Qn, reset
  J_K_Flip_Flop #(.trigger("falling")) j_k_ff_2 (
    .J(1'b1), .clk(out_3), .K(1'b1), .Q(out_4), .preset(and_1_out));  // open: Qn, reset
  J_K_Flip_Flop #(.trigger("falling")) j_k_ff_3 (
    .J(1'b1), .clk(out_4), .K(1'b1), .Q(out_5), .reset(and_1_out));  // open: Qn, preset
  J_K_Flip_Flop #(.trigger("falling")) j_k_ff_4 (
    .J(1'b1), .clk(out_5), .K(1'b1), .Q(out_6), .reset(and_1_out));  // open: Qn, preset
  and and_1 (and_1_out, out_6, out_5, out_4, ~out_3);  // AND_Gate
  Hex_Digit_Display hex_digit_display_1 (.value({out_6, out_5, out_4, out_3}));  // open: dp

  // Notes on the sheet:
  //   Contador de 3-13
  //   Samuel Matias Almeida Irineu - INFO 2
endmodule
