// Logisim project Flip-Flop.circ as structural Verilog: 1 circuit
module circuit (
  input  S,
  input  CK,
  input  in_3,
  input  in_4,
  input  R,
  input  in_6,
  input  in_7,
  input  J,
  input  CK_2,
  input  K,
  input  in_11,
  input  in_12,
  input  in_13,
  input  in_14,
  input  in_15,
  input  in_16,
  input  in_17,
  input  in_18,
  output Q,
  output Q_2,
  output Q_3,
  output Q_4,
  output Q_5,
  output Q_6,
  output Q_7,
  output Q_8,
  output out_27,
  output out_28,
  output out_29,
  output out_30,
  output out_31,
  output out_32,
  output out_33,
  output out_34,
  output out_35,
  output out_36,
  output out_37,
  output out_38,
  output out_39,
  output out_40,
  output out_41
);

  wire and_1_out, and_2_out, and_3_out, clock_1_out, clock_2_out, clock_3_out, clock_4_out, clock_5_out,
       clock_6_out, nand_1_out, nand_2_out, nand_3_out, nand_4_out, nand_7_out, nand_8_out, nand_9_out,
       nand_10_out, not_1_out, not_2_out;

  nand nand_1 (nand_1_out, S, CK);
  nand nand_2 (nand_2_out, CK, R);
  nand nand_3 (nand_3_out, J, Q_8, CK_2);
  nand nand_4 (nand_4_out, CK_2, Q_7, K);
  Clock clock_1 (.out(clock_1_out));
  nand nand_5 (Q, nand_1_out, Q_4);
  nand nand_6 (Q_4, Q, nand_2_out);
  nand nand_7 (nand_7_out, nand_3_out, nand_8_out);
  nand nand_8 (nand_8_out, nand_7_out, nand_4_out);
  J_K_Flip_Flop j_k_ff_1 (.J(in_11), .clk(clock_1_out), .K(in_12), .Q(out_29));  // open: Qn, preset, reset
  Clock clock_2 (.out(clock_2_out));
  Clock clock_3 (.out(clock_3_out));
  not not_1 (not_1_out, CK_2);
  J_K_Flip_Flop j_k_ff_2 (.J(1'b1), .clk(out_29), .K(1'b1), .Q(out_28));  // open: Qn, preset, reset
  J_K_Flip_Flop #(.trigger("falling"), .NegatePresetClear("true")) j_k_ff_3 (
    .J(in_13), .clk(clock_2_out), .K(in_14), .Q(out_30), .reset(not_2_out));  // open: Qn, preset
  J_K_Flip_Flop j_k_ff_4 (.J(in_15), .clk(clock_3_out), .K(in_16), .Q(out_34), .preset(and_2_out));  // open: Qn, reset
  J_K_Flip_Flop j_k_ff_5 (.J(1'b1), .clk(out_28), .K(1'b1), .Q(out_27));  // open: Qn, preset, reset
  J_K_Flip_Flop #(.trigger("falling"), .NegatePresetClear("true")) j_k_ff_6 (
    .J(1'b1), .clk(out_30), .K(1'b1), .Q(out_31), .reset(not_2_out));  // open: Qn, preset
  J_K_Flip_Flop j_k_ff_7 (.J(1'b1), .clk(out_34), .K(1'b1), .Q(out_35), .preset(and_2_out));  // open: Qn, reset
  Clock clock_4 (.out(clock_4_out));
  nand nand_9 (nand_9_out, nand_7_out, not_1_out);
  nand nand_10 (nand_10_out, not_1_out, nand_8_out);
  J_K_Flip_Flop #(.trigger("falling")) j_k_ff_8 (
    .J(in_17), .clk(clock_4_out), .K(in_18), .Q(out_38), .reset(and_3_out));  // open: Qn, preset
  J_K_Flip_Flop #(.trigger("falling"), .NegatePresetClear("true")) j_k_ff_9 (
    .J(1'b1), .clk(out_31), .K(1'b1), .Q(out_32), .reset(not_2_out));  // open: Qn, preset
  J_K_Flip_Flop j_k_ff_10 (.J(1'b1), .clk(out_35), .K(1'b1), .Q(out_36), .reset(and_2_out));  // open: Qn, preset
  J_K_Flip_Flop #(.trigger("falling")) j_k_ff_11 (
    .J(1'b1), .clk(out_38), .K(1'b1), .Q(out_39), .preset(and_3_out));  // open: Qn, reset
  nand nand_11 (Q_7, nand_9_out, Q_8);
  nand nand_12 (Q_8, Q_7, nand_10_out);
  J_K_Flip_Flop #(.trigger("falling"), .NegatePresetClear("true")) j_k_ff_12 (
    .J(1'b1), .clk(out_32), .K(1'b1), .Q(out_33), .reset(not_2_out));  // open: Qn, preset
  J_K_Flip_Flop j_k_ff_13 (.J(1'b1), .clk(out_36), .K(1'b1), .Q(out_37), .preset(and_2_out));  // open: Qn, reset
  Clock clock_5 (.out(clock_5_out));
  Clock clock_6 (.out(clock_6_out));
  J_K_Flip_Flop #(.trigger("falling")) j_k_ff_14 (
    .J(1'b1), .clk(out_39), .K(1'b1), .Q(out_40), .reset(and_3_out));  // open: Qn, preset
  S_R_Flip_Flop s_r_ff_1 (.S(in_3), .clk(clock_5_out), .R(in_4), .Q(Q_2), .Qn(Q_3));  // open: preset, reset
  J_K_Flip_Flop j_k_ff_15 (.J(in_6), .clk(clock_6_out), .K(in_7), .Q(Q_5), .Qn(Q_6));  // open: preset, reset
  and and_1 (and_1_out, out_32, out_33);
  not not_2 (not_2_out, and_1_out);
  J_K_Flip_Flop #(.trigger("falling")) j_k_ff_16 (
    .J(1'b1), .clk(out_40), .K(1'b1), .Q(out_41), .reset(and_3_out));  // open: Qn, preset
  and and_2 (and_2_out, ~out_37, ~out_36, ~out_35, ~out_34);  // AND_Gate
  and and_3 (and_3_out, out_41, out_40, out_39, out_38);

  // Notes on the sheet:
  //   FF-SR Circuito
  //   FF-JK Circuito
  //   Contador 7-0
  //   Contador 11-0
  //   Contador 0-11
  //   FF-SR
  //   Contador 2-14
  //   FF-JK
endmodule
