// Logisim project Flip-Flops_Registradores.circ as structural Verilog: 3 circuits, main circuit Q2
module Q2 (
  input  clock,
  input  D3,
  input  D2,
  input  D1,
  input  D0,
  input  reset,
  output Q3,
  output Q2,
  output Q1,
  output Q0
);

  D_Flip_Flop #(.Pre_Clr_Positions("LEGACY"), .NewFFLayout("false")) d_ff_1 (
    .clk(clock), .D(D3), .Q(Q3), .reset(reset));  // open: Qn, preset
  D_Flip_Flop #(.Pre_Clr_Positions("LEGACY"), .NewFFLayout("false")) d_ff_2 (
    .clk(clock), .D(D2), .Q(Q2), .reset(reset));  // open: Qn, preset
  D_Flip_Flop #(.Pre_Clr_Positions("LEGACY"), .NewFFLayout("false")) d_ff_3 (
    .clk(clock), .D(D1), .Q(Q1), .reset(reset));  // open: Qn, preset
  D_Flip_Flop #(.Pre_Clr_Positions("LEGACY"), .NewFFLayout("false")) d_ff_4 (
    .clk(clock), .D(D0), .Q(Q0), .reset(reset));  // open: Qn, preset
endmodule

module Q3 (
  input  in_1,
  input  in_2,
  input  in_3,
  input  in_4,
  input  in_5,
  input  [3:0] in_6,
  input  in_7,
  output out_8,
  output out_9,
  output out_10,
  output out_11,
  output [3:0] out_12
);

  wire d_ff_1_q, d_ff_2_q, d_ff_3_q, d_ff_4_q;
  wire [3:0] register_1_q;

  D_Flip_Flop #(.Pre_Clr_Positions("LEGACY"), .NewFFLayout("false")) d_ff_1 (
    .clk(in_1), .D(in_2), .Q(d_ff_1_q));  // open: Qn, preset, reset
  D_Flip_Flop #(.Pre_Clr_Positions("LEGACY"), .NewFFLayout("false")) d_ff_2 (
    .clk(in_1), .D(in_3), .Q(d_ff_2_q));  // open: Qn, preset, reset
  D_Flip_Flop #(.Pre_Clr_Positions("LEGACY"), .NewFFLayout("false")) d_ff_3 (
    .clk(in_1), .D(in_4), .Q(d_ff_3_q));  // open: Qn, preset, reset
  D_Flip_Flop #(.Pre_Clr_Positions("LEGACY"), .NewFFLayout("false")) d_ff_4 (
    .clk(in_1), .D(in_5), .Q(d_ff_4_q));  // open: Qn, preset, reset
  Register #(.width(4), .Select("low")) register_1 (.D(in_6), .Q(register_1_q), .clk(in_7));  // open: en, clr
  Register #(.width(4), .Select("low")) register_2 (.D(register_1_q), .Q(out_12), .clk(in_7));  // open: en, clr
  D_Flip_Flop #(.Pre_Clr_Positions("LEGACY"), .NewFFLayout("false")) d_ff_5 (
    .clk(in_1), .D(d_ff_1_q), .Q(out_8));  // open: Qn, preset, reset
  D_Flip_Flop #(.Pre_Clr_Positions("LEGACY"), .NewFFLayout("false")) d_ff_6 (
    .clk(in_1), .D(d_ff_2_q), .Q(out_9));  // open: Qn, preset, reset
  D_Flip_Flop #(.Pre_Clr_Positions("LEGACY"), .NewFFLayout("false")) d_ff_7 (
    .clk(in_1), .D(d_ff_3_q), .Q(out_10));  // open: Qn, preset, reset
  D_Flip_Flop #(.Pre_Clr_Positions("LEGACY"), .NewFFLayout("false")) d_ff_8 (
    .clk(in_1), .D(d_ff_4_q), .Q(out_11));  // open: Qn, preset, reset
endmodule

module Q1 (
  input  clock,
  input  D,
  input  preset,
  input  reset,
  input  enable,
  output Q,
  output Q_prime
);

  D_Flip_Flop #(.Pre_Clr_Positions("LEGACY"), .enable("true"), .NewFFLayout("false")) d_ff_1 (
    .clk(clock), .D(D), .Q(Q), .Qn(Q_prime), .preset(preset), .en(enable), .reset(reset));
endmodule
