// Logisim project Memorias.circ as structural Verilog: 1 circuit, main circuit main
module main (
  input  clock_MAR,
  input  clock_RAM,
  input  cir_RAM,
  input  buffer_RAM,
  input  clock_Out,
  input  [7:0] Input,
  input  clock_In,
  input  buffer_In
);

  wire [7:0] In_q, MAR_q, ram_1_data;

  Register #(.Select("low")) MAR (.D(ram_1_data), .Q(MAR_q), .clk(clock_MAR));  // open: en, clr
  Register #(.Select("low")) In (.D(Input), .Q(In_q), .clk(clock_In));  // open: en, clr
  RAM #(.simpleMode("false"), .Select("low")) ram_1 (
    .addr(MAR_q), .data(ram_1_data), .clk(clock_RAM), .ld(buffer_RAM), .clr(cir_RAM));  // open: sel
  assign ram_1_data = buffer_In ? In_q : 8'bz;  // Controlled_Buffer controlled_buffer_1
  Register #(.Select("low")) Out (.D(ram_1_data), .clk(clock_Out));  // open: en, Q, clr
endmodule
