// Logisim project Registrador.circ as structural Verilog: 1 circuit, main circuit main
module main (
  input  A,
  input  B,
  input  C,
  input  D,
  input  S0,
  input  S1,
  input  Sheft_Right,
  input  Sheft_Left,
  input  Clear,
  output QA,
  output QB,
  output QC,
  output QD
);

  wire CK_out, multiplexer_1_out, multiplexer_2_out, multiplexer_3_out, multiplexer_4_out;

  Clock CK (.out(CK_out));
  Multiplexer #(.select(2), .enable("false")) multiplexer_1 (
    .in0(QA), .in1(Sheft_Right), .in2(QB), .in3(A), .out(multiplexer_1_out), .sel({S1, S0}));
  D_Flip_Flop d_ff_1 (.clk(CK_out), .D(multiplexer_1_out), .Q(QA), .reset(Clear));  // open: Qn, preset
  Multiplexer #(.select(2), .enable("false")) multiplexer_2 (
    .in0(QB), .in1(QA), .in2(QC), .in3(B), .out(multiplexer_2_out), .sel({S1, S0}));
  D_Flip_Flop d_ff_2 (.clk(CK_out), .D(multiplexer_2_out), .Q(QB), .reset(Clear));  // open: Qn, preset
  Multiplexer #(.select(2), .enable("false")) multiplexer_3 (
    .in0(QC), .in1(QB), .in2(QD), .in3(C), .out(multiplexer_3_out), .sel({S1, S0}));
  D_Flip_Flop d_ff_3 (.clk(CK_out), .D(multiplexer_3_out), .Q(QC), .reset(Clear));  // open: Qn, preset
  Multiplexer #(.select(2), .enable("false")) multiplexer_4 (
    .in0(QD), .in1(QC), .in2(Sheft_Left), .in3(D), .out(multiplexer_4_out), .sel({S1, S0}));
  D_Flip_Flop d_ff_4 (.clk(CK_out), .D(multiplexer_4_out), .Q(QD), .reset(Clear));  // open: Qn, preset

  // Notes on the sheet:
  //   Samuel Matias Almeida Irineu - INFO2
endmodule
