// Logisim project Subtrator.circ as structural Verilog: 1 circuit, main circuit main
module main (
  input  A,
  input  B,
  input  VemUm,
  input  A_2,
  input  A_3,
  input  A_4,
  input  B_2,
  input  B_3,
  input  A_5,
  input  VaiUm,
  input  B_4,
  input  B_5
);

  wire and_1_out, and_2_out, and_3_out, and_4_out, and_5_out, and_6_out, and_7_out, and_8_out, and_9_out,
       and_10_out, and_11_out, and_12_out, and_13_out, and_14_out, and_15_out, or_1_out, or_2_out, or_3_out,
       or_4_out, or_5_out, xor_1_out, xor_2_out, xor_3_out, xor_4_out, xor_5_out, xor_6_out, xor_7_out,
       xor_8_out, xor_9_out, xor_10_out, xor_11_out, xor_12_out, xor_13_out, xor_14_out;

  LED u_VaiUm (.in(or_1_out));
  or or_1 (or_1_out, and_1_out, and_2_out, and_3_out);
  or or_2 (or_2_out, and_4_out, and_5_out, and_6_out);
  and and_1 (and_1_out, A, B);
  and and_2 (and_2_out, A, VemUm);
  and and_3 (and_3_out, B, VemUm);
  and and_4 (and_4_out, A_2, xor_1_out);
  and and_5 (and_5_out, A_2, or_3_out);
  and and_6 (and_6_out, xor_1_out, or_3_out);
  xor xor_1 (xor_1_out, B_2, VaiUm);
  xor xor_2 (xor_2_out, B, A);
  xor xor_3 (xor_3_out, VemUm, xor_2_out);
  LED Soma (.in(xor_3_out));
  xor xor_4 (xor_4_out, xor_1_out, A_2);
  xor xor_5 (xor_5_out, or_3_out, xor_4_out);
  LED Soma_2 (.in(xor_5_out));
  or or_3 (or_3_out, and_7_out, and_8_out, and_9_out);
  and and_7 (and_7_out, A_3, xor_6_out);
  and and_8 (and_8_out, A_3, or_4_out);
  and and_9 (and_9_out, xor_6_out, or_4_out);
  xor xor_6 (xor_6_out, B_3, VaiUm);
  xor xor_7 (xor_7_out, xor_6_out, A_3);
  xor xor_8 (xor_8_out, or_4_out, xor_7_out);
  LED Soma_3 (.in(xor_8_out));
  or or_4 (or_4_out, and_10_out, and_11_out, and_12_out);
  and and_10 (and_10_out, A_4, xor_9_out);
  and and_11 (and_11_out, A_4, or_5_out);
  and and_12 (and_12_out, xor_9_out, or_5_out);
  xor xor_9 (xor_9_out, B_4, VaiUm);
  xor xor_10 (xor_10_out, xor_9_out, A_4);
  xor xor_11 (xor_11_out, or_5_out, xor_10_out);
  LED Soma_4 (.in(xor_11_out));
  or or_5 (or_5_out, and_13_out, and_14_out, and_15_out);
  and and_13 (and_13_out, A_5, xor_12_out);
  and and_14 (and_14_out, A_5, VaiUm);
  and and_15 (and_15_out, xor_12_out, VaiUm);
  xor xor_12 (xor_12_out, B_5, VaiUm);
  xor xor_13 (xor_13_out, xor_12_out, A_5);
  xor xor_14 (xor_14_out, VaiUm, xor_13_out);
  LED Soma_5 (.in(xor_14_out));
endmodule
