// Logisim project ULA.circ as structural Verilog: 1 circuit, main circuit main
module main (
  input  [15:0] A,
  input  [15:0] B,
  input  S0,
  input  S2,
  input  S1,
  output [15:0] out_6,
  output [15:0] out_7,
  output [15:0] out_8
);

  wire [15:0] and_1_out, and_2_out, and_3_out, not_1_out, not_2_out, not_3_out, or_1_out, or_2_out, xor_1_out;

  assign not_1_out = ~{16{S0}};  // NOT_Gate not_1, 16 bits wide
  assign not_2_out = ~B;  // NOT_Gate not_2, 16 bits wide
  assign and_1_out = A & B;  // AND_Gate and_1, 16 bits wide
  assign or_1_out = A | B;  // OR_Gate or_1, 16 bits wide
  assign xor_1_out = A ^ B;  // XOR_Gate xor_1, 16 bits wide
  assign not_3_out = ~A;  // NOT_Gate not_3, 16 bits wide
  assign and_2_out = B & not_1_out;  // AND_Gate and_2, 16 bits wide
  assign and_3_out = not_2_out & {16{S0}};  // AND_Gate and_3, 16 bits wide
  assign or_2_out = and_2_out | and_3_out;  // OR_Gate or_2, 16 bits wide
  Multiplexer #(.select(2), .width(16), .enable("false")) multiplexer_1 (
    .in0(and_1_out), .in1(or_1_out), .in2(xor_1_out), .in3(not_3_out), .out(out_8), .sel({S1, S0}));
  Adder #(.width(16)) adder_1 (.a(A), .b(or_2_out), .out(out_6), .cin(S0));  // open: cout
  Multiplexer #(.width(16), .enable("false")) multiplexer_2 (.in0(out_6), .in1(out_8), .out(out_7), .sel(S2));

  // Notes on the sheet:
  //   Samuel Matias - INFO2
endmodule
